# Fritzing sketch Breadboard (saved by Fritzing 0.9.3b)
breadboards: 1

parts:
  LED1 = LED - 5mm [color="Red (633nm)" package="5 mm [THT]"]
  LED2 = LED - 5mm [color="Yellow (595nm)" package="5 mm [THT]"]
  LED3 = LED - 5mm [color="Green (555nm)" package="5 mm [THT]"]
  R1 = Resistor [tolerance=±5% resistance=220 package=THT]
  R2 = Resistor [tolerance=±5% resistance=220 package=THT]
  R3 = Resistor [tolerance=±5% resistance=220 package=THT]
  RE1 = Rotary Encoder [package=THT]
  Raspberry_Pi_1 = Raspberry Pi 3 [part_number=RPI-3-V1.2]
  Part1 = Arduino Uno (Rev3)
  Grove1 = Grove 4 Digit Display

nets:
  GND: LED1.cathode, LED2.cathode, LED3.cathode, Part1.GND, Grove1.GND
  N1: LED1.anode, R1.Pin_0
  N2: LED2.anode, R2.Pin_0
  N3: LED3.anode, R3.Pin_0
  N4: R1.Pin_1, Part1.D10_PWM/SS
  N5: R2.Pin_1, Part1.D9_PWM
  N6: R3.Pin_1, Part1.D8
  N7: RE1.EncoderPinC, Raspberry_Pi_1.GIPO17, Raspberry_Pi_1.GND, Raspberry_Pi_1.GIPO18
  N8: Part1.D2, Grove1.CLK
  N9: Part1.D3_PWM, Grove1.DIO
  5V: Part1.5V, Grove1.VCC
